# Fritzing sketch photoresistor (saved by Fritzing 0.3.8b)
breadboards: 1

parts:
  Arduino1 = Arduino
  R1 = 220 Ω Resistor [package=THT]
  R2 = Basic Photo-Resistor (Photocell) [package=THT]
  LED1 = Red LED - 5mm

nets:
  N1: Arduino1.GND, R2.pin_1, LED1.cathode
  N2: Arduino1.D13, LED1.anode
  N3: Arduino1.+5V, R1.Pin_0
  N4: Arduino1.A0, R1.Pin_1, R2.pin_0
