# Fritzing sketch servo (saved by Fritzing 0.3.8b)
breadboards: 1

parts:
  Arduino1 = Arduino
  J1 = Basic Servo
  R1 = Rotary Potentiometer (Large) [package=THT]

nets:
  N1: Arduino1.D2, J1.pulse
  N2: Arduino1.A0, R1.wiper
  N3: J1.gnd, R1.leg1
  N4: J1.vcc, R1.leg2
