# Fritzing sketch line-follower-1 (saved by Fritzing 0.3.8b)
breadboards: 1

parts:
  U1 = Mystery Part - 3 pins [package=THT]
  U1_2 = Mystery Part - 3 pins [package=THT]
  U1_3 = Mystery Part - 3 pins [package=THT]
  Arduino1 = Arduino
  S2 = Pushbutton [package=THT]
  LED1 = Red LED - 5mm
  R2 = 330 Ω Resistor [package=THT]
  R4 = 10k Ω Resistor [package=THT]

nets:
  N1: U1.leg1, Arduino1.D5
  N2: U1.leg2, U1_2.leg2, U1_3.leg2, Arduino1.+5V, S2.Pin_3, S2.Pin_4
  N3: U1.leg3, U1_2.leg3, U1_3.leg3, Arduino1.GND, LED1.cathode, R4.Pin_1
  N4: U1_2.leg1, Arduino1.D6
  N5: U1_3.leg1, Arduino1.D7
  N6: Arduino1.D8, R2.Pin_0
  N7: Arduino1.D2, S2.Pin_1, S2.Pin_2, R4.Pin_0
  N8: LED1.anode, R2.Pin_1
