# Fritzing sketch pong (saved by Fritzing 0.3.8b)
breadboards: 1

parts:
  Arduino1 = Arduino
  R1 = Rotary Potentiometer (Large) [package=THT]
  R2 = Rotary Potentiometer (Large) [package=THT]

nets:
  N1: Arduino1.GND, R1.leg2, R2.leg2
  N2: Arduino1.A0, R1.wiper
  N3: Arduino1.A1, R2.wiper
  N4: R1.leg1, R2.leg1
