# Fritzing sketch sos (saved by Fritzing 0.3.8b)
breadboards: 1

parts:
  Arduino1 = Arduino
  R2 = 330 Ω Resistor [package=THT]
  LED1 = Red LED - 5mm
  R2_2 = 330 Ω Resistor [package=THT]
  LED2 = yellow LED - 5mm

nets:
  N1: Arduino1.GND, LED1.cathode, LED2.cathode
  N2: Arduino1.D10, R2_2.Pin_0
  N3: Arduino1.D9, R2.Pin_0
  N4: R2.Pin_1, LED2.anode
