# Fritzing sketch sketch (saved by Fritzing 0.3.8b)
breadboards: 1

parts:
  Arduino1 = Arduino
  R1 = Rotary Potentiometer (Large) [package=THT]
  R1_2 = Rotary Potentiometer (Large) [package=THT]

nets:
  N1: Arduino1.GND, R1.leg1, R1_2.leg1
  N2: Arduino1.+5V, R1.leg2, R1_2.leg2
  N3: Arduino1.A0, R1.wiper
  N4: Arduino1.A1, R1_2.wiper
